# Fritzing sketch SRC Schematic (saved by Fritzing 0.9.9b)
breadboards: 1

parts:
  Teensy_3_1 = Teensy 3.1
  WIZ820io2 = WIZ820io [part_number=WIZ820io]
  Part2 = 12 NeoPixel Ring [part_number=1643]
  DFRobot_DFPlayer_Mini1 = DFRobot DFPlayer Mini [part_number=DFR0299]
  SP1 = SPEAKER [package=pcb_mount_speaker]  # not connected
  Part3 = BME280 Breakout
  OLED_I2C1 = OLED 128x64 I2C Monochrome Display
  S1 = Pushbutton [package="[THT]"]
  R1 = Resistor [tolerance=±5% resistance=10k package="0603 [SMD]"]

nets:
  GND: Teensy_3_1.GND, WIZ820io2.GND, Part3.GND, OLED_I2C1.GND
  VIN: Teensy_3_1.A11, WIZ820io2.VIN, Part3.3.3V, OLED_I2C1.VDD, S1.Pin_3, S1.Pin_4
  VDD: Part2.VDD, DFRobot_DFPlayer_Mini1.VCC
  N1: Part2.GND, DFRobot_DFPlayer_Mini1.GND-1, DFRobot_DFPlayer_Mini1.GND-2, R1.Pin_0
  N2: S1.Pin_1, S1.Pin_2, R1.Pin_1

custom parts:
  12 NeoPixel Ring: 12 ultra bright smart LED NeoPixels are arranged in a circle with 1.5" (37mm) outer diameter. The rings are 'chainable' - connect the output pin of one to the input pin of another. Use only one microcontroller pin to control as many as you can chain together! Each LED is addressable as the driver chip is inside the LED. Each one has ~18mA constant current drive so the color will be very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
  Pushbutton: A generic pushbutton.

// code stored in the sketch: L03_01_button.ino
  const int LEDPIN = 23;
  int i; 
void setup() {
  i = digitalRead(23);
  Serial.begin (9600);
  while (!Serial);
  Serial.print("i");
}

void loop() {
    for (i){
    Serial.print(i);  
    delay(printDelay);
   }
}
